# Fritzing sketch esquema (saved by Fritzing 0.9.3b)
breadboards: 1

parts:
  Raspberry_Pi1 = Raspberry Pi B+
  J1 = T Cobbler Plus

nets:
  3V3: Raspberry_Pi1.3v3, Raspberry_Pi1.3V3, J1.3.3V
  N1: Raspberry_Pi1.GPIO2, J1.GPIO_2
  N2: Raspberry_Pi1.GPIO3, J1.GPIO_3
  N3: Raspberry_Pi1.GPIO4, J1.GPIO_4
  GND: Raspberry_Pi1.GND, J1.GND
  N4: Raspberry_Pi1.GPIO17, J1.GPIO_17
  N5: Raspberry_Pi1.GPIO27, J1.GPIO_27
  N6: Raspberry_Pi1.GPIO22, J1.GPIO_22
  N7: Raspberry_Pi1.GPIO10, J1.GPIO_10
  N8: Raspberry_Pi1.GPIO9, J1.GPIO_9
  N9: Raspberry_Pi1.GPIO11, J1.GPIO_11
  N10: Raspberry_Pi1.ID_SD, J1.ID_SD
  N11: Raspberry_Pi1.GPIO5, J1.GPIO_5
  N12: Raspberry_Pi1.GPIO6, J1.GPIO_6
  N13: Raspberry_Pi1.GPIO13, J1.GPIO_13
  N14: Raspberry_Pi1.GPIO19, J1.GPIO_19
  N15: Raspberry_Pi1.GPIO26, J1.GPIO_26
  N16: Raspberry_Pi1.GPIO21, J1.GPIO_21
  N17: Raspberry_Pi1.GPIO20, J1.GPIO_20
  N18: Raspberry_Pi1.GPIO16, J1.GPIO_16
  N19: Raspberry_Pi1.GPIO12, J1.GPIO_12
  N20: Raspberry_Pi1.ID_SC, J1.ID_SC
  N21: Raspberry_Pi1.GPIO7, J1.GPIO_7
  N22: Raspberry_Pi1.GPIO8, J1.GPIO_8
  N23: Raspberry_Pi1.GPIO25, J1.GPIO_25
  N24: Raspberry_Pi1.GPIO24, J1.GPIO_24
  N25: Raspberry_Pi1.GPIO23, J1.GPIO_23
  N26: Raspberry_Pi1.GPIO18, J1.GPIO_18
  N27: Raspberry_Pi1.GPIO15, J1.GPIO_15
  N28: Raspberry_Pi1.GPIO14, J1.GPIO_14
  5V: Raspberry_Pi1.5V, J1.5V

custom parts:
  T Cobbler Plus: The T-Cobbler Plus is an add on prototyping board from Adafruit specifically designed for the Raspberry Pi B+ that can break out all those tasty power, GPIO, I2C and SPI pins from the 40-pin header onto a solderless breadboard. This set will make "cobbling together" prototypes with the Pi super easy. The T-Cobbler Plus can plug into any solderless breadboard.
